// Logisim project alu-control.circ as structural Verilog: 1 circuit, main circuit main
module main (
  input  [1:0] Opcode,
  input  [5:0] Funct,
  input  [1:0] sh,
  output [3:0] ALUControl
);

  wire comparator_1_eq, comparator_2_eq, comparator_3_eq, comparator_4_eq, comparator_5_eq, comparator_6_eq,
       comparator_7_eq, comparator_8_eq, comparator_9_eq, comparator_10_eq, comparator_11_eq,
       comparator_12_eq, comparator_13_eq, comparator_14_eq, comparator_15_eq, comparator_15_gt;
  wire [3:0] Ctrl;
  wire [31:0] add, AND, asr, lsl, lsr, NOT, OR, sub, XOR;
  wire [31:4] multiplexer_1_out;

  Comparator #(.width(2)) comparator_1 (.a(Opcode), .b(2'b00), .eq(comparator_1_eq));  // open: gt, lt
  Comparator #(.width(2)) comparator_2 (.a(Opcode), .b(2'b10), .eq(comparator_2_eq));  // open: gt, lt
  Comparator #(.width(2)) comparator_3 (.a(Opcode), .b(2'b01), .eq(comparator_3_eq));  // open: gt, lt
  Comparator #(.width(4)) comparator_4 (.a(Funct[4:1]), .b(4'b0100), .eq(comparator_4_eq));  // open: gt, lt
  Comparator #(.width(4)) comparator_5 (.a(Funct[4:1]), .b(4'b0010), .eq(comparator_5_eq));  // open: gt, lt
  Comparator #(.width(4)) comparator_6 (.a(Funct[4:1]), .b(4'b0000), .eq(comparator_6_eq));  // open: gt, lt
  Comparator #(.width(4)) comparator_7 (.a(Funct[4:1]), .b(4'b0001), .eq(comparator_7_eq));  // open: gt, lt
  Comparator #(.width(4)) comparator_8 (.a(Funct[4:1]), .b(4'b1100), .eq(comparator_8_eq));  // open: gt, lt
  Comparator #(.width(4)) comparator_9 (.a(Funct[4:1]), .b(4'b1111), .eq(comparator_9_eq));  // open: gt, lt
  Comparator #(.width(4)) comparator_10 (.a(Funct[4:1]), .b(4'b1010), .eq(comparator_10_eq));  // open: gt, lt
  Comparator #(.width(4)) comparator_11 (.a(Funct[4:1]), .b(4'b1101), .eq(comparator_11_eq));  // open: gt, lt
  Comparator #(.width(2)) comparator_12 (.a(sh), .b(2'b00), .eq(comparator_12_eq));  // open: gt, lt
  Comparator #(.width(2)) comparator_13 (.a(sh), .b(2'b01), .eq(comparator_13_eq));  // open: gt, lt
  Comparator #(.width(2)) comparator_14 (.a(sh), .b(2'b10), .eq(comparator_14_eq));  // open: gt, lt
  Comparator #(.width(1)) comparator_15 (
    .a(Funct[0]), .b(1'b0), .gt(comparator_15_gt), .eq(comparator_15_eq));  // open: lt
  Multiplexer #(.select(4), .width(32)) multiplexer_1 (
    .in0(AND), .in1(OR), .in2(XOR), .in3(NOT), .in4(lsl), .in5(lsr), .in6(asr), .in7(add), .in8(sub),
    .out({multiplexer_1_out, ALUControl}), .sel(Ctrl));  // open: in9, in10, in11, in12, in13, in14, in15, en
  // Pins of 4 and 32 bits meet at {multiplexer_1_out, ALUControl}

  // Notes on the sheet:
  //   DO NOT MOVE, CHANGE, ADD, OR REMOVE INPUTS AND OUTPUTS!!!
endmodule
