// Logisim project alu.circ as structural Verilog: 2 circuits, main circuit main
module main (
  input  [31:0] A,
  input  [31:0] B,
  input  [3:0] ALUControl,
  output [3:0] ALUFlags,
  output [31:0] Result
);

  wire and_1_out, and_2_out, comparator_1_eq, comparator_2_eq, comparator_3_eq, comparator_5_eq,
       comparator_6_eq, or_1_out, or_3_out, xor_1_out, xor_2_out;
  wire [31:0] add, AND, asr, lsl, lsr, NOT, OR, sub, XOR;

  xor xor_1 (xor_1_out, A[31], B[31]);
  Comparator #(.width(4)) comparator_1 (.a(ALUControl), .b(4'b1000), .eq(comparator_1_eq));  // open: gt, lt
  Comparator #(.width(1)) comparator_2 (.a(A[31]), .b(B[31]), .eq(comparator_2_eq));  // open: gt, lt
  Adder #(.width(32)) adder_1 (.a(A), .b(B), .out(add), .cout(ALUFlags[1]));  // open: cin
  Subtractor #(.width(32)) subtractor_1 (.a(A), .b(B), .out(sub));  // open: bin, bout
  and and_1 (and_1_out, xor_1_out, comparator_1_eq);
  Comparator #(.width(4)) comparator_3 (.a(ALUControl), .b(4'b0111), .eq(comparator_3_eq));  // open: gt, lt
  xor xor_2 (xor_2_out, A[31], Result[31]);
  and and_2 (and_2_out, comparator_2_eq, comparator_3_eq);
  Multiplexer #(.select(4), .width(32)) multiplexer_1 (
    .in0(AND), .in1(OR), .in2(XOR), .in3(NOT), .in4(lsl), .in5(lsr), .in6(asr), .in7(add), .in8(sub),
    .out(Result), .sel(ALUControl));  // open: in9, in10, in11, in12, in13, in14, in15, en
  or or_1 (or_1_out, and_1_out, and_2_out);
  Comparator #(.width(32)) comparator_4 (.a(Result), .b({32{1'b0}}), .eq(ALUFlags[2]), .lt(ALUFlags[3]));  // open: gt
  Shifter #(.width(32)) shifter_1 (.in(B), .\dist (A[4:0]), .out(lsl));
  Shifter #(.width(32), .shift("lr")) shifter_2 (.in(B), .\dist (A[4:0]), .out(lsr));
  Comparator #(.width(4)) comparator_5 (.a(ALUControl), .b(4'b0111), .eq(comparator_5_eq));  // open: gt, lt
  Comparator #(.width(4)) comparator_6 (.a(ALUControl), .b(4'b1000), .eq(comparator_6_eq));  // open: gt, lt
  Shifter #(.width(32), .shift("ar")) shifter_3 (.in(B), .\dist (A[4:0]), .out(asr));
  assign OR = A | B;  // OR_Gate or_2, 32 bits wide
  or or_3 (or_3_out, comparator_5_eq, comparator_6_eq);
  assign AND = A & B;  // AND_Gate and_3, 32 bits wide
  assign XOR = A ^ B;  // XOR_Gate xor_3, 32 bits wide
  and and_4 (ALUFlags[0], or_1_out, xor_2_out, or_3_out);
  assign NOT = ~A;  // NOT_Gate not_1, 32 bits wide

  // Other names for the same wires on the sheet: oVerflow = ALUFlags[0]; Carry = ALUFlags[1]; Zero = ALUFlags[2];
  //   Negative = ALUFlags[3]; Ctrl[3:0] = ALUControl

  // Notes on the sheet:
  //   INPUTS to your circuit
  //   DON'T CHANGE THE LOCATIONS OF THE INPUTS AND OUTPUTS!
  //   OUTPUTS from your circuit
endmodule

module overflow (
);

  wire and_1_out, and_2_out, comparator_1_gt, comparator_1_lt, comparator_2_gt, comparator_2_lt,
       comparator_3_gt, comparator_3_lt, oVerflow;
  wire [31:0] A, B, result;

  Comparator #(.width(32)) comparator_1 (
    .a(A), .b({32{1'b0}}), .gt(comparator_1_gt), .lt(comparator_1_lt));  // open: eq
  Comparator #(.width(32)) comparator_2 (
    .a(B), .b({32{1'b0}}), .gt(comparator_2_gt), .lt(comparator_2_lt));  // open: eq
  and and_1 (and_1_out, comparator_1_lt, comparator_2_gt);
  and and_2 (and_2_out, comparator_1_gt, comparator_2_lt);
  Comparator #(.width(32)) comparator_3 (
    .a(result), .b({32{1'b0}}), .gt(comparator_3_gt), .lt(comparator_3_lt));  // open: eq
  and and_3 (oVerflow, comparator_1_gt, and_2_out, comparator_3_lt);
  and and_4 (oVerflow, comparator_3_gt, and_1_out, comparator_1_lt);
endmodule
