// Logisim project control.circ as structural Verilog: 2 circuits, main circuit main
module main (
  input  Op,
  input  Funct5,
  input  Funct0,
  input  Funct5_2,
  input  Funct0_2,
  output ALUSrc,
  output MemW,
  output ALUSrc_2,
  output ImmSrcRight,
  output RegW,
  output RegSrcRight,
  output ALUOp
);

  wire and_1_out;

  and and_1 (and_1_out, Op, Funct0);
  or or_1 (ALUSrc, Funct5, and_1_out);

  assign ALUSrc_2 = 1'b1;
endmodule

module main2 (
  input  OpR,
  input  Funct5,
  input  Funct0,
  output MemToReg,
  output MemW,
  output ALUSrc,
  output ImmSrcRight,
  output RegW,
  output RegSrcRight,
  output ALUOp
);


  assign ALUSrc = 1'b1;
endmodule
