// Logisim project cpu.circ as structural Verilog: 1 circuit, main circuit main
module main (
  input  [31:0] INSTRUCTION,
  input  CLOCK,
  output [31:0] FETCH_ADDRESS,
  output [31:0] R0_Value,
  output [31:0] R1_Value,
  output [31:0] R2_Value,
  output [31:0] LR_Value,
  output [31:0] SP_Value
);

  wire main_1_p1, main_1_p2, main_1_p4, main_1_p5, main_1_p18, main_1_p23;
  wire [3:0] main_3_alucontrol;
  wire [31:0] adder_1_out, bit_extender_1_out, main_1_p9, main_1_p20, main_1_p21, multiplexer_1_out;

  Register #(.width(32)) PC (.D(adder_1_out), .Q(FETCH_ADDRESS), .clk(CLOCK));  // open: en, clr
  Adder #(.width(32)) adder_1 (.a(FETCH_ADDRESS), .b(32'h4), .out(adder_1_out));  // open: cin, cout
  assign bit_extender_1_out = {{24{1'b0}}, INSTRUCTION[7:0]};  // Bit_Extender bit_extender_1
  // regfile_main main_1: pin names not known; wires that end beside it: main_1_p1, main_1_p2, main_1_p2, main_1_p4, main_1_p5, INSTRUCTION[19:16], INSTRUCTION[3:0], INSTRUCTION[15:12], main_1_p9, main_1_p4, R0_Value, R1_Value, 1'b1, main_1_p5, R2_Value, CLOCK, LR_Value, main_1_p18, SP_Value, main_1_p20, main_1_p21, main_1_p18, main_1_p23, main_1_p23, main_1_p1
  Multiplexer #(.width(32)) multiplexer_1 (
    .in0(main_1_p21), .in1(bit_extender_1_out), .out(multiplexer_1_out), .sel(1'b1));  // open: en
  alu_main main_2 (
    .ALUControl(main_3_alucontrol), .A(main_1_p20), .Result(main_1_p9), .B(multiplexer_1_out));  // open: ALUFlags
  alu_control_main main_3 (
    .Opcode(INSTRUCTION[27:26]), .Funct(INSTRUCTION[25:20]), .sh(INSTRUCTION[6:5]),
    .ALUControl(main_3_alucontrol));

  // Other names for the same wires on the sheet: clk = CLOCK; fetch_addr[31:0] = FETCH_ADDRESS;
  //   funct[5:0] = INSTRUCTION[25:20]; Rm[3:0] = INSTRUCTION[3:0]; sh[1:0] = INSTRUCTION[6:5];
  //   Rd[3:0] = INSTRUCTION[15:12]; Rn[3:0] = INSTRUCTION[19:16]; Op[1:0] = INSTRUCTION[27:26];
  //   cond[3:0] = INSTRUCTION[31:28]; R0[31:0] = R0_Value; R1[31:0] = R1_Value; R2[31:0] = R2_Value;
  //   R13[31:0] = SP_Value; R14[31:0] = LR_Value

  // Notes on the sheet:
  //   Output
  //   Inputs
  //   These are DEBUG/TEST outputs from your circuit.
endmodule
