// Logisim project alu-control.circ as structural Verilog: 1 circuit, main circuit main
module main (
  input  [1:0] Opcode,
  input  [5:0] Funct,
  input  [1:0] sh,
  output [3:0] ALUControl
);

  wire alucontrol_1_p4, alucontrol_1_p5, alucontrol_1_p6, alucontrol_1_p7, alucontrol_1_p8, alucontrol_1_p9,
       alucontrol_1_p10, alucontrol_1_p11, alucontrol_1_p12;

  // ALUControl alucontrol_1: pin names not known; wires that end beside it: Opcode, Funct, sh, alucontrol_1_p4, alucontrol_1_p5, alucontrol_1_p6, alucontrol_1_p7, alucontrol_1_p8, alucontrol_1_p9, alucontrol_1_p10, alucontrol_1_p11, alucontrol_1_p12
  // ALUEncoder aluencoder_1: pin names not known; wires that end beside it: alucontrol_1_p4, alucontrol_1_p5, alucontrol_1_p6, alucontrol_1_p7, alucontrol_1_p8, alucontrol_1_p9, alucontrol_1_p10, alucontrol_1_p11, alucontrol_1_p12, ALUControl

  // Notes on the sheet:
  //   DO NOT MOVE, CHANGE, ADD, OR REMOVE INPUTS AND OUTPUTS!!!
endmodule
