// Logisim project alu.circ as structural Verilog: 1 circuit, main circuit main
module main (
  input  [31:0] A,
  input  [31:0] B,
  input  [3:0] ALUControl,
  output [3:0] ALUFlags,
  output [31:0] Result
);

  // ALU alu_1: pin names not known; wires that end beside it: A, B, ALUControl, ALUFlags, Result

  // Other names for the same wires on the sheet: oVerflow = ALUFlags[0]; Carry = ALUFlags[1]; Zero = ALUFlags[2];
  //   Negative = ALUFlags[3]; Ctrl[3:0] = ALUControl

  // Notes on the sheet:
  //   INPUTS to your circuit
  //   DON'T CHANGE THE LOCATIONS OF THE INPUTS AND OUTPUTS!
  //   OUTPUTS from your circuit
endmodule
